# Fritzing sketch hardware (saved by Fritzing 0.8.7b)
circuit board: 5cm x 5cm
breadboards: 1

parts:
  Power_plug1 = Power plug
  R1 = Resistor [tolerance=±5% resistance=82k package=THT]
  R3 = Resistor [tolerance=±5% resistance=1.5k package=THT]
  R4 = Resistor [tolerance=±5% resistance=27k package=THT]
  D1 = Rectifier Diode [part_number=1N4007 package="300 mil [THT]"]
  JP2 = Header 2 [package=jst-2-pth-kit]
  U2 = TRANSISTOR_NPN_2 [part_number=2N2222A package=to-92]
  U1 = RJ11 Jack [package=rj11-6]
  R2 = Resistor [tolerance=±5% resistance=2.2k package=THT]
  Raspberry_Pi_B_rev1 = Raspberry Pi B rev2
  U3 = TRANSISTOR_NPN_2 [part_number=2N2222A package=to-92]
  U4 = TRANSISTOR_NPN_2 [part_number=2N2222A package=to-92]
  Q4 = npn-Powertransistor [part_number=TIP122 package="TO220 [THT]"]

nets:
  GND: Power_plug1.GND, U1.4, R2.Pin_1, Raspberry_Pi_B_rev1.GND, U3.E, Q4.emitter
  N1: Power_plug1.VCC, R3.Pin_0, R4.Pin_1, JP2.2
  N2: R1.Pin_0, U2.B
  N3: R1.Pin_1, U1.3, Raspberry_Pi_B_rev1.GPIO_18
  N4: R3.Pin_1, U4.C
  N5: R4.Pin_0, U2.C, U4.B
  N6: D1.cathode, U3.C, Q4.base
  N7: D1.anode, U4.E
  N8: JP2.1, Q4.collector
  N9: U2.E, R2.Pin_0, U3.B
